// Digital circuit alu-extended.dig as structural Verilog
module alu_extended (
  input  [15:0] A,
  input  [2:0] ALUOP,
  input  [15:0] B,
  output [15:0] RESULT,
  output [3:0] FLAG
);

  wire add_1_c_o, add_2_c_o, and_2_out, and_3_out, and_4_out, and_5_out, and_6_out, and_7_out, and_8_out,
       and_9_out, and_10_out, and_11_out, not_1_out, not_2_out, not_3_out, not_4_out, not_5_out, not_6_out,
       not_7_out, sub_1_c_o;
  wire [15:0] add_1_s, and_1_out, nand_1_out, nor_1_out, or_1_out, sub_1_s, xnor_1_out, xor_1_out;

  not not_1 (not_1_out, A[15]);
  Add #(.Bits(16)) add_1 (.a(A), .b(B), .c_i(1'b0), .s(add_1_s), .c_o(add_1_c_o));
  Sub #(.Bits(16)) sub_1 (.a(A), .b(B), .c_i(1'b0), .s(sub_1_s), .c_o(sub_1_c_o));
  assign and_1_out = A & B;  // And and_1, 16 bits wide
  assign or_1_out = A | B;  // Or or_1, 16 bits wide
  assign xor_1_out = A ^ B;  // XOr xor_1, 16 bits wide
  assign nand_1_out = ~(A & B);  // NAnd nand_1, 16 bits wide
  assign nor_1_out = ~(A | B);  // NOr nor_1, 16 bits wide
  assign xnor_1_out = ~(A ^ B);  // XNOr xnor_1, 16 bits wide
  not not_2 (not_2_out, B[15]);
  not not_3 (not_3_out, ALUOP[0]);
  not not_4 (not_4_out, ALUOP[1]);
  not not_5 (not_5_out, ALUOP[2]);
  and and_2 (and_2_out, B[15], A[15]);
  and and_3 (and_3_out, not_2_out, not_1_out);
  and and_4 (and_4_out, A[15], not_2_out);
  and and_5 (and_5_out, B[15], not_1_out);
  and and_6 (and_6_out, not_3_out, not_4_out, not_5_out);
  and and_7 (and_7_out, not_5_out, not_4_out, ALUOP[0]);
  Multiplexer #(.Selector_Bits(3), .Bits(16)) multiplexer_1 (
    .sel(ALUOP), .in_0(add_1_s), .in_1(sub_1_s), .in_2(and_1_out), .in_3(or_1_out), .in_4(xor_1_out),
    .in_5(nand_1_out), .in_6(nor_1_out), .in_7(xnor_1_out), .out({FLAG[1], RESULT[14:0]}));
  not not_6 (not_6_out, FLAG[1]);
  not not_7 (not_7_out, sub_1_c_o);
  and and_8 (and_8_out, not_6_out, and_2_out, and_6_out);
  and and_9 (and_9_out, FLAG[1], and_3_out, and_6_out);
  and and_10 (and_10_out, not_6_out, and_4_out, and_7_out);
  and and_11 (and_11_out, FLAG[1], and_5_out, and_7_out);
  Add #(.Bits(16)) add_2 (.a({FLAG[1], RESULT[14:0]}), .b({16{1'b1}}), .c_i(1'b0), .c_o(add_2_c_o));  // open: s
  Multiplexer #(.Selector_Bits(3)) multiplexer_2 (
    .sel(ALUOP), .in_0(add_1_c_o), .in_1(not_7_out), .in_2(1'b0), .in_3(1'b0), .in_4(1'b0), .in_5(1'b0),
    .in_6(1'b0), .in_7(1'b0), .out(FLAG[2]));
  or or_2 (FLAG[3], and_8_out, and_9_out, and_10_out, and_11_out);
  not not_8 (FLAG[0], add_2_c_o);
  // NotConnected on nothing

  assign RESULT[15] = FLAG[1];

  // Notes on the sheet:
  //   A: First input to ALU
  //   ALUOP: Operation selection input
  //   RESULT: The result of this ALU operation
  //   FLAG: The flags associated with the result of this ALU operation
  //   0. Z (zero)
  //   1. N (negative)
  //   2. C (carry)
  //   3. V (overflow)
  //   B: Second input to ALU
endmodule

/* Test case RESULT:
ALUOP A B RESULT

# Test small results
loop(a, 1 << 4)
loop(b, 1 << 4)
    (00) (a) (b) ((a + b) & 0xFFFF)
    (01) (a) (b) ((a - b) & 0xFFFF)
    (10) (a) (b) (a & b)
    (11) (a) (b) (a | b)
end loop
end loop


# Test large results
loop(i, 1000)
    let a = random(1 << 16);
    let b = random(1 << 16);

    (00) (a) (b) ((a + b) & 0xFFFF)
    (01) (a) (b) ((a - b) & 0xFFFF)
    (10) (a) (b) (a & b)
    (11) (a) (b) (a | b)
end loop
*/

/* Test case Z:
ALUOP A B Z

declare Z = FLAG & 0b1;

# Test all zero cases
00 0 0 1
01 0 0 1
10 0 0 1
11 0 0 1

# Test 1 + (-1) = 0
00 1 0xFFFF 1

# Test with a single bit set in A
loop(s, 16)
    let a = 1 << s;

    00 (a) 0 (a = 0)
    01 (a) 0 (a = 0)
    10 (a) 0 1
    11 (a) 0 (a = 0)
end loop

# Test random inputs
loop(i, 200)
    let a = random(1 << 16);
    let b = random(1 << 16);

    00 (a) (b) (((a + b) & 0xFFFF) = 0)
    01 (a) (b) (((a - b) & 0xFFFF) = 0)
    10 (a) (b) ((a & b) = 0)
    11 (a) (b) ((a | b) = 0)
end loop
*/

/* Test case N:
ALUOP A B N

declare N = (FLAG >> 1) & 0b1;

# Test all zero cases
00 0 0 0
01 0 0 0
10 0 0 0
11 0 0 0

00 1 0xFFFF 0

# Test with a single bit set in A
loop(s, 16)
    let a = 1 << s;

    00 (a) 0 ((a >> 15) & 0b1)
    01 (a) 0 ((a >> 15) & 0b1)
    10 (a) 0 0
    11 (a) 0 ((a >> 15) & 0b1)
end loop

# Test random inputs
loop(i, 200)
    let a = random(1 << 16);
    let b = random(1 << 16);

    00 (a) (b) (((a + b) >> 15) & 0b1)
    01 (a) (b) (((a - b) >> 15) & 0b1)
    10 (a) (b) (((a & b) >> 15) & 0b1)
    11 (a) (b) (((a | b) >> 15) & 0b1)
end loop
*/

/* Test case C:
ALUOP A B C

declare C = (FLAG >> 2) & 0b1;

00 0 0 0

# (0 - 0) is implemented as 0 + (0xFFFF + 1), so a carry is expected
01 0 0 1

# Carry should propagate all the way from the first bit if necessary
00 1 0xFFFF 1

# Test with a single bit set in A
loop(s, 16)
    let a = 1 << s;

    00 (a) 0 0
    01 (a) 0 1  # (a - 0) is implemented as (a + 0xFFFF + 1) in the adder, so a carry is always expected
    10 (a) 0 0  # carry is defined as 0 for AND
    11 (a) 0 0  # carry is defined as 0 for OR
end loop

# Adding 15 bit values should never carry
loop(i, 100)
    00 (random(1 << 15)) (random(1 << 15)) 0
end loop

# Test random inputs
loop(i, 200)
    let a = random(1 << 16);
    let b = random(1 << 16);

    00 (a) (b) (((a + b) >> 16) & 0b1)
    01 (a) (b) (~((a - b) >> 16) & 0b1)
end loop

# AND and OR never set carry
loop(i, 100)
    let a = random(1 << 16);
    let b = random(1 << 16);
    10 (a) (b) 0
    11 (a) (b) 0
end loop
*/

/* Test case V:
ALUOP A B V

declare V = (FLAG >> 3) & 0b1;

00 0 0 0
01 0 0 0

# 1 + (-1) = 0  ; different input signs = no overflow here!
00 1 0xFFFF 0

# 3 - 5 = 3 + (-5) = -2  ; subtraction inverts the second operand sign
01 3 5 0

# Some edge cases when subtracting 0x8000
01 0x8000 0x8000 0
01 0xFFFF 0x8000 0
01 0x7FFF 0x8000 1

# Test with a single bit set in A
loop(s, 16)
    let a = 1 << s;

    00 (a) 0 0
    01 (a) 0 0
    10 (a) 0 0  # overflow is defined as 0 for AND
    11 (a) 0 0  # overflow is defined as 0 for OR
end loop

# Test random inputs
loop(i, 200)
    let a = random(1 << 16);
    let b = random(1 << 16);

    00 (a) (b) (((~(a ^ b) & (a ^ (a + b))) >> 15) & 0b1)
    01 (a) (b) (((~(a ^ -b) & (a ^ (a - b))) >> 15) & 0b1)
end loop

# AND and OR never set overflow
loop(i, 100)
    let a = random(1 << 16);
    let b = random(1 << 16);
    10 (a) (b) 0
    11 (a) (b) 0
end loop
*/
