// Digital circuit control_unit-extended.dig as structural Verilog
module control_unit_extended (
  input  [15:0] INST,
  input  NOEXEC,
  output [2:0] ALUOP,
  output [2:0] RS1,
  output [2:0] RS2,
  output [2:0] WS,
  output STR,
  output WE,
  output [1:0] DMUX,
  output LDR,
  output immB,
  output immA,
  output [2:0] RS3,
  output jcc,
  output push,
  output pop,
  output smov,
  output SETH,
  output call,
  output [15:0] nextI,
  output nextcounter,
  output [15:0] nextI2,
  output tmpreg
);

  wire and_1_out, and_6_out, lastbit, movl, not_1_out, not_2_out, not_3_out, not_4_out, not_5_out, not_6_out,
       not_7_out, not_8_out, not_9_out, not_10_out, not_11_out, not_12_out, not_13_out, not_14_out, or_6_out,
       or_7_out, or_8_out, str_t;
  wire [0:0] or_2_out, or_3_out;
  wire [1:0] and_12_out;
  wire [1:1] or_9_out;
  wire [2:0] demultiplexer_1_out_0, demultiplexer_1_out_1, multiplexer_1_out_2, notconnected_1_out,
       notconnected_2_out, notconnected_3_out, notconnected_4_out;
  wire [11:0] multiplexer_1_out;
  wire [15:0] notconnected_5_out;

  and and_1 (and_1_out, NOEXEC, INST[11]);
  Multiplexer #(.Bits(16)) multiplexer_1 (
    .sel(and_1_out), .in_0(INST), .in_1({16{1'b0}}),
    .out({lastbit, multiplexer_1_out_2, multiplexer_1_out[11:8], immA, multiplexer_1_out[6:0]}));
  or or_1 (immB, multiplexer_1_out[3], call);
  Demultiplexer #(.Bits(3)) demultiplexer_1 (
    .sel(lastbit), .in(multiplexer_1_out_2), .out_0(demultiplexer_1_out_0), .out_1(demultiplexer_1_out_1));
  not not_1 (not_1_out, demultiplexer_1_out_0[1]);
  not not_2 (not_2_out, demultiplexer_1_out_0[0]);
  not not_3 (not_3_out, demultiplexer_1_out_0[2]);
  not not_4 (not_4_out, demultiplexer_1_out_0[1]);
  not not_5 (not_5_out, lastbit);
  not not_6 (not_6_out, demultiplexer_1_out_0[2]);
  not not_7 (not_7_out, demultiplexer_1_out_0[1]);
  not not_8 (not_8_out, demultiplexer_1_out_0[0]);
  not not_9 (not_9_out, demultiplexer_1_out_0[2]);
  not not_10 (not_10_out, demultiplexer_1_out_0[2]);
  not not_11 (not_11_out, demultiplexer_1_out_0[0]);
  and and_2 (str_t, demultiplexer_1_out_0[2], not_1_out, not_2_out);
  and and_3 (LDR, demultiplexer_1_out_0[0], demultiplexer_1_out_0[2]);
  and and_4 (movl, not_3_out, not_4_out, not_5_out);
  and and_5 (SETH, not_6_out, not_7_out, demultiplexer_1_out_0[0]);
  not not_12 (not_12_out, multiplexer_1_out[0]);
  and and_6 (and_6_out, not_8_out, demultiplexer_1_out_0[1], demultiplexer_1_out_0[2]);
  and and_7 (pop, demultiplexer_1_out_0[2], demultiplexer_1_out_0[1], demultiplexer_1_out_0[0]);
  and and_8 (smov, not_9_out, demultiplexer_1_out_0[1], demultiplexer_1_out_0[0]);
  and and_9 (jcc, not_10_out, not_11_out, demultiplexer_1_out_0[1]);
  and and_10 (call, multiplexer_1_out[0], and_6_out);
  and and_11 (push, not_12_out, and_6_out);
  Multiplexer #(.Selector_Bits(2), .Bits(3)) multiplexer_2 (
    .sel({call, jcc}), .in_0(multiplexer_1_out[10:8]), .in_1(3'b000), .in_2(3'b100),
    .in_3(notconnected_1_out), .out(WS));
  // NotConnected on notconnected_1_out
  or or_2 (or_2_out[0], push, pop);
  Multiplexer #(.Selector_Bits(2), .Bits(3)) multiplexer_3 (
    .sel({call, or_2_out[0]}), .in_0(multiplexer_1_out[6:4]), .in_1(3'b110), .in_2(3'b111),
    .in_3(notconnected_2_out), .out(RS1));
  // NotConnected on notconnected_2_out
  Multiplexer #(.Selector_Bits(2), .Bits(3)) multiplexer_4 (
    .sel({call, or_3_out[0]}), .in_0(multiplexer_1_out[2:0]), .in_1(multiplexer_1_out[10:8]), .in_2(3'b001),
    .in_3(notconnected_3_out), .out(RS2));
  or or_3 (or_3_out[0], push, str_t);
  // NotConnected on notconnected_3_out
  or or_4 (STR, str_t, push, SETH);
  Multiplexer #(.Bits(3)) multiplexer_5 (
    .sel(str_t), .in_0(multiplexer_1_out[10:8]), .in_1(multiplexer_1_out[2:0]), .out(RS3));
  or or_5 (WE, movl, lastbit, or_6_out, jcc, LDR);
  or or_6 (or_6_out, call, smov);
  and and_12 (and_12_out[0], LDR, not_13_out);
  or or_7 (or_7_out, lastbit, or_8_out, jcc);
  or or_8 (or_8_out, call, smov);
  Multiplexer #(.Selector_Bits(2), .Bits(2)) multiplexer_6 (
    .sel(and_12_out), .in_0(2'b00), .in_1(2'b01), .in_2(2'b10), .in_3(2'b00), .out(DMUX));
  and and_13 (and_12_out[1], movl, not_14_out);
  not not_13 (not_13_out, or_7_out);
  not not_14 (not_14_out, or_7_out);
  or or_9 (or_9_out[1], call, push, pop, smov);
  Multiplexer #(.Selector_Bits(2), .Bits(3)) multiplexer_7 (
    .sel({or_9_out[1], jcc}), .in_0(demultiplexer_1_out_1), .in_1(3'b001), .in_2(3'b000),
    .in_3(notconnected_4_out), .out(ALUOP));
  // NotConnected on notconnected_4_out
  Multiplexer #(.Selector_Bits(2), .Bits(16)) multiplexer_8 (
    .sel({jcc, call}), .in_0({16{1'b0}}), .in_1(16'h6400), .in_2({9'h11e, multiplexer_1_out[10:8], 4'b0000}),
    .in_3(notconnected_5_out), .out(nextI));
  // NotConnected on notconnected_5_out
  Multiplexer #(.Bits(16)) multiplexer_9 (
    .sel(call), .in_0({16{1'b0}}), .in_1({9'h10e, multiplexer_1_out[10:8], 4'b0000}), .out(nextI2));
  or or_10 (nextcounter, call, jcc);

  assign tmpreg = call;

  // Notes on the sheet:
  //   Rd
  //   Ra
  //   Z
  //   Rb
endmodule

/* Test case All Tests:
	INST                                    WE  ALUOP  RS1   RS2  WS  STR  LDR DMUX

let aluop  = 0b1000;
let ldrop  = 0b0101;
let strop  = 0b0100;
let movlop = 0b0000;

loop(rd, 1<<3)
loop(ra, 1<<3)
loop(rb, 1<<3)

loop(i, 4)
	((aluop+i)<<12 | rd<<8 | ra<<4 | rb<<0) 1  (i)     (ra)  (rb) (rd)  0   X    0  #test add/sub/and/orr
end loop

	(ldrop    <<12 | rd<<8 | ra<<4 )        1  X       (ra)  x    (rd)  0   1    1  #test ldr
	(strop    <<12 | rd<<8 | ra<<4 )        0  X       (ra)  (rd)  X    1   X    X  #test str
	
	let imm = random(256);
	(movlop   <<12 | rd<<8 | imm )          1  X       X      X   (rd)  0   X    2  #test movl

end loop
end loop
end loop
*/

/* Test case WS:
	INST                                    WS 

let aluop  = 0b1000;
let ldrop  = 0b0101;
let strop  = 0b0100;
let movlop = 0b0000;

loop(rd, 1<<3)
loop(ra, 1<<3)
loop(rb, 1<<3)

loop(i, 4)
	((aluop+i)<<12 | rd<<8 | ra<<4 | rb<<0) (rd)  #test add/sub/and/orr
end loop

	(ldrop    <<12 | rd<<8 | ra<<4 )        (rd)   #test ldr
	(strop    <<12 | rd<<8 | ra<<4 )        X     #test str
	
	let imm = random(256);
	(movlop   <<12 | rd<<8 | imm )          (rd)  #test movl

end loop
end loop
end loop
*/

/* Test case RS1:
	INST                                    RS1  

let aluop  = 0b1000;
let ldrop  = 0b0101;
let strop  = 0b0100;
let movlop = 0b0000;

loop(rd, 1<<3)
loop(ra, 1<<3)
loop(rb, 1<<3)

loop(i, 4)
	((aluop+i)<<12 | rd<<8 | ra<<4 | rb<<0) (ra)  #test add/sub/and/orr
end loop

	(ldrop    <<12 | rd<<8 | ra<<4 )        (ra)  #test ldr
	(strop    <<12 | rd<<8 | ra<<4 )        (ra)  #test str

end loop
end loop
end loop
*/

/* Test case RS2:
	INST                                    RS2  

let aluop  = 0b1000;
let ldrop  = 0b0101;
let strop  = 0b0100;
let movlop = 0b0000;

loop(rd, 1<<3)
loop(ra, 1<<3)
loop(rb, 1<<3)

loop(i, 4)
	((aluop+i)<<12 | rd<<8 | ra<<4 | rb<<0) (rb) #test add/sub/and/orr
end loop
	(strop    <<12 | rd<<8 | ra<<4 )        (rd) #test str

end loop
end loop
end loop
*/

/* Test case STR:
	INST                                    STR 

let aluop  = 0b1000;
let ldrop  = 0b0101;
let strop  = 0b0100;
let movlop = 0b0000;

loop(rd, 1<<3)
loop(ra, 1<<3)
loop(rb, 1<<3)

loop(i, 4)
	((aluop+i)<<12 | rd<<8 | ra<<4 | rb<<0) 0  #test add/sub/and/orr
end loop

	(ldrop    <<12 | rd<<8 | ra<<4 )        0  #test ldr
	(strop    <<12 | rd<<8 | ra<<4 )        1  #test str
	
	let imm = random(256);
	(movlop   <<12 | rd<<8 | imm )          0  #test movl

end loop
end loop
end loop
*/

/* Test case DMUX:
	INST                                    DMUX

let aluop  = 0b1000;
let ldrop  = 0b0101;
let strop  = 0b0100;
let movlop = 0b0000;

loop(rd, 1<<3)
loop(ra, 1<<3)
loop(rb, 1<<3)

loop(i, 4)
	((aluop+i)<<12 | rd<<8 | ra<<4 | rb<<0) 0  #test add/sub/and/orr
end loop

	(ldrop    <<12 | rd<<8 | ra<<4 )        1  #test ldr
	
	let imm = random(256);
	(movlop   <<12 | rd<<8 | imm )          2  #test movl

end loop
end loop
end loop
*/

/* Test case LDR:
	INST                                    LDR 

let aluop  = 0b1000;
let ldrop  = 0b0101;
let strop  = 0b0100;
let movlop = 0b0000;

loop(rd, 1<<3)
loop(ra, 1<<3)
loop(rb, 1<<3)

loop(i, 4)
	((aluop+i)<<12 | rd<<8 | ra<<4 | rb<<0) X    #test add/sub/and/orr
end loop

	(ldrop    <<12 | rd<<8 | ra<<4 )        1    #test ldr
	(strop    <<12 | rd<<8 | ra<<4 )        X    #test str
	
	let imm = random(256);
	(movlop   <<12 | rd<<8 | imm )          X    #test movl

end loop
end loop
end loop
*/

/* Test case ALUOP:
	INST                                    ALUOP 

let aluop  = 0b1000;
let ldrop  = 0b0101;
let strop  = 0b0100;
let movlop = 0b0000;

loop(rd, 1<<3)
loop(ra, 1<<3)
loop(rb, 1<<3)

loop(i, 4)
	((aluop+i)<<12 | rd<<8 | ra<<4 | rb<<0) (i)    #test add/sub/and/orr
end loop

end loop
end loop
end loop
*/

/* Test case WE:
	INST                                    WE  

let aluop  = 0b1000;
let ldrop  = 0b0101;
let strop  = 0b0100;
let movlop = 0b0000;

loop(rd, 1<<3)
loop(ra, 1<<3)
loop(rb, 1<<3)

loop(i, 4)
	((aluop+i)<<12 | rd<<8 | ra<<4 | rb<<0) 1  #test add/sub/and/orr
end loop

	(ldrop    <<12 | rd<<8 | ra<<4 )        1  #test ldr
	(strop    <<12 | rd<<8 | ra<<4 )        0  #test str
	
	let imm = random(256);
	(movlop   <<12 | rd<<8 | imm )          1  #test movl

end loop
end loop
end loop
*/
