// Digital circuit control_unit1.dig as structural Verilog
module control_unit1 (
  input  [15:0] INST,
  input  NOEXEC,
  output [1:0] ALUOP,
  output [2:0] RS1,
  output [2:0] RS2,
  output [2:0] WS,
  output STR,
  output WE,
  output [1:0] DMUX,
  output LDR,
  output SETH,
  output immB,
  output immA
);

  wire and_1_out, and_2_out, and_4_out, not_1_out, not_2_out, not_3_out, not_4_out, not_5_out, not_6_out,
       not_7_out;
  wire [1:0] and_6_out;
  wire [2:0] demultiplexer_1_out_0, multiplexer_1_out;
  wire [2:2] demultiplexer_1_out_1;
  wire [15:4] multiplexer_1_out_2;

  and and_1 (and_1_out, NOEXEC, INST[11]);
  Multiplexer #(.Bits(16)) multiplexer_1 (
    .sel(and_1_out), .in_0(INST), .in_1({16{1'b0}}),
    .out({multiplexer_1_out_2[15:11], WS, immA, multiplexer_1_out_2[6:4], immB, multiplexer_1_out}));
  Demultiplexer #(.Bits(3)) demultiplexer_1 (
    .sel(multiplexer_1_out_2[15]), .in(multiplexer_1_out_2[14:12]), .out_0(demultiplexer_1_out_0),
    .out_1({demultiplexer_1_out_1[2], ALUOP}));
  and and_2 (and_2_out, demultiplexer_1_out_0[2], not_1_out);
  not not_1 (not_1_out, demultiplexer_1_out_0[0]);
  and and_3 (LDR, demultiplexer_1_out_0[0], demultiplexer_1_out_0[2]);
  and and_4 (and_4_out, not_2_out, not_4_out);
  not not_2 (not_2_out, demultiplexer_1_out_0[2]);
  not not_3 (not_3_out, demultiplexer_1_out_0[1]);
  not not_4 (not_4_out, multiplexer_1_out_2[15]);
  and and_5 (SETH, not_5_out, demultiplexer_1_out_0[0]);
  not not_5 (not_5_out, demultiplexer_1_out_0[2]);
  Multiplexer #(.Bits(3)) multiplexer_2 (.sel(and_4_out), .in_0(multiplexer_1_out_2[6:4]), .in_1(3'b000), .out(RS1));
  not not_6 (not_6_out, multiplexer_1_out_2[15]);
  not not_7 (not_7_out, multiplexer_1_out_2[15]);
  or or_1 (STR, and_2_out, SETH);
  or or_2 (WE, LDR, and_4_out, multiplexer_1_out_2[15]);
  and and_6 (and_6_out[0], LDR, not_6_out);
  and and_7 (and_6_out[1], and_4_out, not_7_out);
  // NotConnected on nothing
  // NotConnected on nothing
  Multiplexer #(.Bits(3)) multiplexer_3 (.sel(STR), .in_0(multiplexer_1_out), .in_1(WS), .out(RS2));
  // NotConnected on nothing
  // NotConnected on nothing
  // NotConnected on nothing
  // NotConnected on nothing
  Multiplexer #(.Selector_Bits(2), .Bits(2)) multiplexer_4 (
    .sel(and_6_out), .in_0(2'b00), .in_1(2'b01), .in_2(2'b10), .in_3(2'b00), .out(DMUX));

  // Notes on the sheet:
  //   Operation to perform
  //   Destination/data register: Which
  //   register the result is written to
  //   Register used for first operand
  //   Register used for second operand
  //   ldr and str set to 0
  //   opcode
  //   Z
  //   Rd
  //   Ra
  //   Rb
endmodule

/* Test case All Tests:
	INST                                    WE  ALUOP  RS1   RS2  WS  STR  LDR DMUX

let aluop  = 0b1000;
let ldrop  = 0b0101;
let strop  = 0b0100;
let movlop = 0b0000;

loop(rd, 1<<3)
loop(ra, 1<<3)
loop(rb, 1<<3)

loop(i, 4)
	((aluop+i)<<12 | rd<<8 | ra<<4 | rb<<0) 1  (i)     (ra)  (rb) (rd)  0   X    0  #test add/sub/and/orr
end loop

	(ldrop    <<12 | rd<<8 | ra<<4 )        1  X       (ra)  x    (rd)  0   1    1  #test ldr
	(strop    <<12 | rd<<8 | ra<<4 )        0  X       (ra)  (rd)  X    1   X    X  #test str
	
	let imm = random(256);
	(movlop   <<12 | rd<<8 | imm )          1  X       X      X   (rd)  0   X    2  #test movl

end loop
end loop
end loop
*/

/* Test case WS:
	INST                                    WS 

let aluop  = 0b1000;
let ldrop  = 0b0101;
let strop  = 0b0100;
let movlop = 0b0000;

loop(rd, 1<<3)
loop(ra, 1<<3)
loop(rb, 1<<3)

loop(i, 4)
	((aluop+i)<<12 | rd<<8 | ra<<4 | rb<<0) (rd)  #test add/sub/and/orr
end loop

	(ldrop    <<12 | rd<<8 | ra<<4 )        (rd)   #test ldr
	(strop    <<12 | rd<<8 | ra<<4 )        X     #test str
	
	let imm = random(256);
	(movlop   <<12 | rd<<8 | imm )          (rd)  #test movl

end loop
end loop
end loop
*/

/* Test case RS1:
	INST                                    RS1  

let aluop  = 0b1000;
let ldrop  = 0b0101;
let strop  = 0b0100;
let movlop = 0b0000;

loop(rd, 1<<3)
loop(ra, 1<<3)
loop(rb, 1<<3)

loop(i, 4)
	((aluop+i)<<12 | rd<<8 | ra<<4 | rb<<0) (ra)  #test add/sub/and/orr
end loop

	(ldrop    <<12 | rd<<8 | ra<<4 )        (ra)  #test ldr
	(strop    <<12 | rd<<8 | ra<<4 )        (ra)  #test str

end loop
end loop
end loop
*/

/* Test case RS2:
	INST                                    RS2  

let aluop  = 0b1000;
let ldrop  = 0b0101;
let strop  = 0b0100;
let movlop = 0b0000;

loop(rd, 1<<3)
loop(ra, 1<<3)
loop(rb, 1<<3)

loop(i, 4)
	((aluop+i)<<12 | rd<<8 | ra<<4 | rb<<0) (rb) #test add/sub/and/orr
end loop
	(strop    <<12 | rd<<8 | ra<<4 )        (rd) #test str

end loop
end loop
end loop
*/

/* Test case STR:
	INST                                    STR 

let aluop  = 0b1000;
let ldrop  = 0b0101;
let strop  = 0b0100;
let movlop = 0b0000;

loop(rd, 1<<3)
loop(ra, 1<<3)
loop(rb, 1<<3)

loop(i, 4)
	((aluop+i)<<12 | rd<<8 | ra<<4 | rb<<0) 0  #test add/sub/and/orr
end loop

	(ldrop    <<12 | rd<<8 | ra<<4 )        0  #test ldr
	(strop    <<12 | rd<<8 | ra<<4 )        1  #test str
	
	let imm = random(256);
	(movlop   <<12 | rd<<8 | imm )          0  #test movl

end loop
end loop
end loop
*/

/* Test case WE:
	INST                                    WE  

let aluop  = 0b1000;
let ldrop  = 0b0101;
let strop  = 0b0100;
let movlop = 0b0000;

loop(rd, 1<<3)
loop(ra, 1<<3)
loop(rb, 1<<3)

loop(i, 4)
	((aluop+i)<<12 | rd<<8 | ra<<4 | rb<<0) 1  #test add/sub/and/orr
end loop

	(ldrop    <<12 | rd<<8 | ra<<4 )        1  #test ldr
	(strop    <<12 | rd<<8 | ra<<4 )        0  #test str
	
	let imm = random(256);
	(movlop   <<12 | rd<<8 | imm )          1  #test movl

end loop
end loop
end loop
*/

/* Test case LDR:
	INST                                    LDR 

let aluop  = 0b1000;
let ldrop  = 0b0101;
let strop  = 0b0100;
let movlop = 0b0000;

loop(rd, 1<<3)
loop(ra, 1<<3)
loop(rb, 1<<3)

loop(i, 4)
	((aluop+i)<<12 | rd<<8 | ra<<4 | rb<<0) X    #test add/sub/and/orr
end loop

	(ldrop    <<12 | rd<<8 | ra<<4 )        1    #test ldr
	(strop    <<12 | rd<<8 | ra<<4 )        X    #test str
	
	let imm = random(256);
	(movlop   <<12 | rd<<8 | imm )          X    #test movl

end loop
end loop
end loop
*/

/* Test case DMUX:
	INST                                    DMUX

let aluop  = 0b1000;
let ldrop  = 0b0101;
let strop  = 0b0100;
let movlop = 0b0000;

loop(rd, 1<<3)
loop(ra, 1<<3)
loop(rb, 1<<3)

loop(i, 4)
	((aluop+i)<<12 | rd<<8 | ra<<4 | rb<<0) 0  #test add/sub/and/orr
end loop

	(ldrop    <<12 | rd<<8 | ra<<4 )        1  #test ldr
	
	let imm = random(256);
	(movlop   <<12 | rd<<8 | imm )          2  #test movl

end loop
end loop
end loop
*/

/* Test case ALUOP:
	INST                                    ALUOP 

let aluop  = 0b1000;
let ldrop  = 0b0101;
let strop  = 0b0100;
let movlop = 0b0000;

loop(rd, 1<<3)
loop(ra, 1<<3)
loop(rb, 1<<3)

loop(i, 4)
	((aluop+i)<<12 | rd<<8 | ra<<4 | rb<<0) (i)    #test add/sub/and/orr
end loop

end loop
end loop
end loop
*/
