// Digital circuit extended-cpu.dig as structural Verilog
module extended_cpu (
  input  CLK
);

  wire and_1_out, and_2_out, and_3_out, call, comparator_1_eq, comparator_2_eq, comparator_3_eq,
       control_unit_extended_1_ldr, f1write, imma, immb, jcc, multiplexer_8_out, nextin, noexec, nopcup,
       not_1_out, not_2_out, not_3_out, not_6_out, or_1_out, or_2_out, or_3_out, pcwrite, pop, push, seth,
       smov, str, tempreg, we;
  wire [1:0] control_unit_extended_1_dmux;
  wire [2:0] aluop, rs1, rs2, rs3, ws;
  wire [3:0] alu_extended_1_flag;
  wire [7:0] multiplexer_13_out;
  wire [15:0] alu_extended_1_result, control_unit_extended_1_nexti, control_unit_extended_1_nexti2, d_ff_1_q,
       d_ff_2_q, FL_q, multiplexer_1_out, multiplexer_2_out, multiplexer_3_out, multiplexer_4_out,
       multiplexer_5_out, multiplexer_6_out, multiplexer_7_out, multiplexer_9_out, multiplexer_10_out,
       multiplexer_11_out, multiplexer_12_out, neg_1_out, notconnected_1_out, PC_q, plus_1_s, plus_2_s,
       RAM_d1, RAM_d2, reg_file_extended_1_out1, reg_file_extended_1_out2, reg_file_extended_1_out3, Stack_q,
       tmpread;
  wire [15:8] multiplexer_13_out_2;

  Multiplexer #(.Selector_Bits(2), .Bits(16)) multiplexer_1 (
    .sel(control_unit_extended_1_dmux), .in_0(alu_extended_1_result), .in_1(RAM_d1),
    .in_2({{8{1'b0}}, multiplexer_13_out}), .in_3(notconnected_1_out), .out(multiplexer_1_out));
  // NotConnected on notconnected_1_out
  // Probe result on alu_extended_1_result
  not not_1 (not_1_out, control_unit_extended_1_dmux[1]);
  not not_2 (not_2_out, control_unit_extended_1_dmux[0]);
  and and_1 (and_1_out, not_1_out, not_2_out);
  alu_extended alu_extended_1 (
    .A(multiplexer_6_out), .ALUOP(aluop), .B(multiplexer_2_out), .RESULT(alu_extended_1_result),
    .FLAG(alu_extended_1_flag));
  or or_1 (or_1_out, and_1_out, f1write);
  and and_2 (and_2_out, immb, and_1_out);
  Multiplexer #(.Bits(16)) multiplexer_2 (
    .sel(and_2_out), .in_0(multiplexer_9_out), .in_1({{13{1'b0}}, rs2}), .out(multiplexer_2_out));
  Multiplexer #(.Bits(16)) multiplexer_3 (.sel(or_2_out), .in_0(Stack_q), .in_1(plus_2_s), .out(multiplexer_3_out));
  Add #(.Bits(16)) plus_2 (.a(multiplexer_7_out), .b(Stack_q), .c_i(1'b0), .s(plus_2_s));  // open: c_o
  Multiplexer #(.Selector_Bits(2), .Bits(16)) multiplexer_4 (
    .sel({nopcup, pcwrite}), .in_0(plus_1_s), .in_1(multiplexer_1_out), .in_2(PC_q),
    .in_3(reg_file_extended_1_out3), .out(multiplexer_4_out));
  Multiplexer #(.Bits(16)) multiplexer_5 (
    .sel(f1write), .in_0({{12{1'b0}}, alu_extended_1_flag}), .in_1(multiplexer_1_out), .out(multiplexer_5_out));
  and and_3 (and_3_out, imma, and_1_out);
  Multiplexer #(.Bits(16)) multiplexer_6 (
    .sel(and_3_out), .in_0(reg_file_extended_1_out1), .in_1({{13{1'b0}}, rs1}), .out(multiplexer_6_out));
  reg_file_extended reg_file_extended_1 (
    .SETH(seth), .IN(multiplexer_1_out), .clk(CLK), .RS1(rs1), .RS2(rs2), .RS3(rs3), .WE(we), .WS(ws),
    .SMOV(smov), .TMPWRITE(tempreg), .f1(FL_q), .PC(PC_q), .Stack(Stack_q), .OUT2(reg_file_extended_1_out2),
    .OUT1(reg_file_extended_1_out1), .OUT3(reg_file_extended_1_out3), .PCWRITE(pcwrite), .f1write(f1write));
  or or_2 (or_2_out, pop, push);
  Multiplexer #(.Bits(16)) multiplexer_7 (.sel(pop), .in_0(neg_1_out), .in_1(16'h1), .out(multiplexer_7_out));
  Add #(.Bits(16)) plus_1 (.a(16'h1), .b(PC_q), .c_i(1'b0), .s(plus_1_s));  // open: c_o
  Multiplexer multiplexer_8 (.sel(str), .in_0(or_1_out), .in_1(1'b0), .out(multiplexer_8_out));
  Multiplexer #(.Selector_Bits(2), .Bits(16)) multiplexer_9 (
    .sel({push, str}), .in_0(reg_file_extended_1_out2), .in_1(reg_file_extended_1_out3), .in_2({16{1'b0}}),
    .in_3({16{1'b1}}), .out(multiplexer_9_out));
  Register #(.Bits(16)) Stack (.D(multiplexer_3_out), .C(CLK), .en(1'b1), .Q(Stack_q));
  Neg #(.Bits(16)) neg_1 (.in(16'h1), .out(neg_1_out));
  Register #(.Bits(16), .isProgramCounter("true")) PC (.D(multiplexer_4_out), .C(CLK), .en(1'b1), .Q(PC_q));
  Register #(.Bits(16)) FL (.D(multiplexer_5_out), .C(CLK), .en(multiplexer_8_out), .Q(FL_q));
  Multiplexer #(.Bits(16)) multiplexer_10 (
    .sel(not_3_out), .in_0(reg_file_extended_1_out2), .in_1(tmpread), .out(multiplexer_10_out));
  not not_3 (not_3_out, comparator_1_eq);
  not not_4 (noexec, FL_q[0]);
  Comparator #(.Bits(16)) comparator_1 (.a(tmpread), .b({16{1'b0}}), .eq(comparator_1_eq));  // open: gt, lt
  D_FF #(.Bits(16)) d_ff_1 (.D(control_unit_extended_1_nexti2), .C(CLK), .Q(d_ff_1_q));  // open: nQ
  Multiplexer #(.Bits(16)) multiplexer_11 (
    .sel(tempreg), .in_0({16{1'b0}}), .in_1(multiplexer_1_out), .out(multiplexer_11_out));
  Multiplexer #(.Bits(16)) multiplexer_12 (
    .sel(nextin), .in_0(d_ff_1_q), .in_1(control_unit_extended_1_nexti), .out(multiplexer_12_out));
  // Probe DATA on PC_q
  Register #(.Bits(16)) TMP (.D(multiplexer_11_out), .C(CLK), .en(1'b1), .Q(tmpread));
  control_unit_extended control_unit_extended_1 (
    .INST({multiplexer_13_out_2, multiplexer_13_out}), .NOEXEC(noexec), .ALUOP(aluop), .RS1(rs1), .RS2(rs2),
    .WS(ws), .STR(str), .WE(we), .DMUX(control_unit_extended_1_dmux), .LDR(control_unit_extended_1_ldr),
    .immB(immb), .immA(imma), .RS3(rs3), .jcc(jcc), .push(push), .pop(pop), .smov(smov), .SETH(seth),
    .call(call), .nextI(control_unit_extended_1_nexti), .nextcounter(nextin),
    .nextI2(control_unit_extended_1_nexti2), .tmpreg(tempreg));
  Comparator #(.Bits(16)) comparator_2 (.a({16{1'b0}}), .b(multiplexer_12_out), .eq(comparator_2_eq));  // open: gt, lt
  D_FF #(.Bits(16)) d_ff_2 (.D(multiplexer_12_out), .C(CLK), .Q(d_ff_2_q));  // open: nQ
  not not_5 (nopcup, comparator_2_eq);
  or or_3 (or_3_out, pop, str);
  RAMDualAccess #(.AddrBits(16), .isProgramMemory("true"), .Bits(16)) RAM (
    .str(or_3_out), .C(CLK), .ld(control_unit_extended_1_ldr), .A1(alu_extended_1_result),
    .Din1(multiplexer_10_out), .A2(PC_q), .D1(RAM_d1), .D2(RAM_d2));
  Comparator #(.Bits(16)) comparator_3 (.a({16{1'b0}}), .b(d_ff_2_q), .eq(comparator_3_eq));  // open: gt, lt
  Multiplexer #(.Bits(16)) multiplexer_13 (
    .sel(not_6_out), .in_0(RAM_d2), .in_1(d_ff_2_q), .out({multiplexer_13_out_2, multiplexer_13_out}));
  not not_6 (not_6_out, comparator_3_eq);

  // Notes on the sheet:
  //   Instruction Storage - For multi-cycle execution
endmodule

/* Test case CPU:
# assert these registers can be tested
CLK R1 R2 R3 R4 FL PC

program(0)  # assert program memory exists
init R1=0;  # assert we can initialise R1
init R2=0;  # assert we can initialise R2
init R3=0;  # assert we can initialise R3
init R4=0;  # assert we can initialise R4
init FL=0;  # assert we can initialise FL
init PC=0;  # assert we can initialise PC

0 0 0 0 0 0 0
*/

/* Test case GP_PC:
CLK     R1     R2     R3     R4     PC

init R1=0x5;
init R2=0x98;
0        x      x      x      x 0x0000
c   0x0005 0x0098      x      x 0x0001
c   0x0005 0x0098      x      x 0x0002
c   0x0005 0x0002      x      x 0x0003
c   0x0005 0x0002      x      x 0x0005

program(0x8000,0x8000,0x8270,0x8710,0x03ff,0x0000)
*/

/* Test case MOVL:
CLK     R1     R2     R3     R4     PC

0        x      x      x      x 0x0000
c   0x00ff      x      x      x 0x0001
c   0x0000      x      x      x 0x0002
c   0x0000 0x000c      x      x 0x0003
c   0x0000 0x000c 0x000d      x 0x0004
c   0x0000 0x000c 0x000d 0x00a3 0x0005

program(0x01ff,0x0100,0x020c,0x030d,0x04a3)
*/

/* Test case READ_FLAGS:
CLK     R1     R2     R3     R4     PC

init R1=0x76;
init R4=0xF;
0        x      x      x      x 0x0000
c   0x0076 0x0000      x 0x000f 0x0001
c   0x0076 0x0000      x 0x000f 0x0002
c   0x0076 0x0000 0x0005 0x000f 0x0003

program(0x9211,0x8350,0xa334)
*/

/* Test case SETH:
CLK     R1     R2     R3     R4     PC

init R1=0xAD;
init R2=0x0D;
init R3=0xEF;
init R4=0xAD;
0        x      x      x      x 0x0000
c   0xdead 0x000d 0x00ef 0x00ad 0x0001
c   0xdead 0xf00d 0x00ef 0x00ad 0x0002
c   0xdead 0xf00d 0xbeef 0x00ad 0x0003
c   0xdead 0xf00d 0xbeef 0x0bad 0x0004

program(0x11de,0x12f0,0x13be,0x140b)
*/

/* Test case FLAGS:
CLK     R1     R2     R3     R4   FLAG     PC

declare FLAG = FL & 0xF;

init R1=1;
init R2=0xFFFF;
init R3=0x7FFF;
init R4=0x8000;
0        x      x      x      x      x 0x0000
c   0x0001 0xffff 0x7fff 0x8000 0x0001 0x0001
c   0x0001 0xffff 0x7fff 0x8000 0x0005 0x0002
c   0x0001 0xffff 0x7fff 0x8000 0x0005 0x0003
c   0x0001 0xffff 0x7fff 0x8000 0x0000 0x0004
c   0x0001 0xffff 0x7fff 0x8000 0x0006 0x0005
c   0x0001 0xffff 0x7fff 0x8000 0x0006 0x0006
c   0x0001 0xffff 0x7fff 0x8000 0x0002 0x0007
c   0x0001 0xffff 0x7fff 0x8000 0x0002 0x0008
c   0x0001 0xffff 0x7fff 0x8000 0x000c 0x0009
c   0x0001 0xffff 0x7fff 0x8000 0x0004 0x000a
c   0x0001 0xffff 0x7fff 0x8000 0x000c 0x000b
c   0x0001 0xffff 0x7fff 0x8000 0x000a 0x000c

program(0x8000,0x8012,0x9011,0x9012,0x8022,0x9021,0x8034,0x8041,0x9041,0x9031,0x9043,0x8013)
*/

/* Test case LDR:
CLK     R1     R2     R3     R4     PC

init R1=0x3;
0        x      x      x      x 0x0000
c   0x0003 0x5200      x      x 0x0001
c   0x0003 0x5200 0x9876      x 0x0002

program(0x5200,0x5310,0x0000,0x9876)
*/

/* Test case ALU:
CLK     R1     R2     R3     R4   FLAG     PC

declare FLAG = FL & 0xF;

init R1=0x1A;
init R2=0xF000;
init R2=0xCDFF;
0        x      x      x      x      x 0x0000
c   0x001a 0xcdff      x 0xce19 0x0002 0x0001
c   0x001a 0xcdff      x 0x001a 0x0000 0x0002
c   0x001a 0xcdff      x 0xcdff 0x0006 0x0003
c   0x001a 0xcdff      x 0x3201 0x0000 0x0004
c   0x001a 0xcdff      x 0x0000 0x0001 0x0005
c   0x001a 0xcdff      x 0x0000 0x0001 0x0006
c   0x001a 0xcdff      x 0xcdff 0x0002 0x0007
c   0x001a 0xcdff      x 0xcdff 0x0002 0x0008
c   0x0000 0xcdff      x 0xcdff 0x0001 0x0009
c   0x0000 0x0000      x 0xcdff 0x0001 0x000a

program(0x8412,0xa421,0x9423,0x9432,0xa413,0xa431,0xb412,0xb012,0x8100,0x8230)
*/

/* Test case STR:
CLK     R1     R2     R3     R4     PC

init R1=0x3;
init R2=0xDAF5;
0        x      x      x      x 0x0000
c   0x0003 0xdaf5      x      x 0x0001
c   0x0003 0xdaf5 0xdaf5      x 0x0002

program(0x4210,0x5310,0x0000,0x0000)
*/

/* Test case JUMPS:
CLK     R1     R2     R3     R4     PC

0        x      x      x      x 0x0000
c        x      x      x 0x0003 0x0001
c   0x0001      x      x 0x0003 0x0002
c   0x0001      x      x 0x0003 0x0005
c   0x0001      x 0x0003 0x0003 0x0006
c   0x0001      x 0x0003 0x0003 0x0003
c   0x0001 0x0003 0x0003 0x0003 0x0004
c   0x0001 0x0003 0x0003 0x0003 0x0007
c   0x0001 0x0003 0x0003 0x0009 0x0008
c   0x0001 0x0003 0x0003 0x0009 0x000a

program(0x0403,0x8170,0x8774,0x0203,0x8772,0x0303,0x9773,0x0409,0x8714,0x8770,0x0000)
*/

/* Test case ADD:
CLK     R1     R2     R3     R4     PC

init R1=0x87;
init R2=0x93;
0        x      x      x      x 0x0000
c   0x0087 0x0093 0x011a      x 0x0001
c   0x0087 0x0093 0x011a 0x01ad 0x0002
c   0x010e 0x0093 0x011a 0x01ad 0x0003

program(0x8321,0x8432,0x8111)
*/

/* Test case REC:
CLK     R1     R2     R3     R4     PC

0        x      x      x      x 0x0000
c        x      x      x 0x0000 0x0001
c   0x0020      x      x 0x0000 0x0002
c   0x0020 0x0008      x 0x0000 0x0003
c   0x0020 0x0008 0x0001 0x0000 0x0004
c   0x0021 0x0008 0x0001 0x0000 0x0005
c   0x0021 0x0008 0x0001 0xffff 0x0006
c   0x0021 0x0008 0x001f 0xffff 0x0007
c   0x0021 0x0008 0x001f 0xffff 0x0008
c   0x0021 0x0008 0x001f 0xffff 0x0009
c   0x0021 0x0008 0x001f 0xffff 0x000a
c   0x0021 0x0008 0x0001 0xffff 0x000b
c   0x0021 0x0008 0x0001 0xfffe 0x000c
c   0x0021 0x0008 0x0001 0xfffe 0x000d
c   0x000f 0x0008 0x0001 0xfffe 0x000e
c   0x000f 0x0008 0x0001 0xfffd 0x000f
c   0x000f 0x0008 0x0001 0xfffd 0x0010
c   0x000f 0x0007 0x0001 0xfffd 0x0011
c   0xfffe 0x0007 0x0001 0xfffd 0x0012
c   0x0021 0x0007 0x0001 0xfffd 0x0013
c   0x0022 0x0007 0x0001 0xfffd 0x0014
c   0x0022 0x0007 0x0001 0xfffc 0x0015
c   0x0022 0x0007 0x0018 0xfffc 0x0016
c   0x0022 0x0007 0x0018 0xfffc 0x0017
c   0x0022 0x0007 0x0018 0xfffc 0x0008
c   0x0022 0x0007 0x0018 0xfffc 0x0009
c   0x0022 0x0007 0x0018 0xfffc 0x000a
c   0x0022 0x0007 0x0001 0xfffc 0x000b
c   0x0022 0x0007 0x0001 0xfffb 0x000c
c   0x0022 0x0007 0x0001 0xfffb 0x000d
c   0x0004 0x0007 0x0001 0xfffb 0x000e
c   0x0004 0x0007 0x0001 0xfffa 0x000f
c   0x0004 0x0007 0x0001 0xfffa 0x0010
c   0x0004 0x0006 0x0001 0xfffa 0x0011
c   0xfffb 0x0006 0x0001 0xfffa 0x0012
c   0x0022 0x0006 0x0001 0xfffa 0x0013
c   0x0023 0x0006 0x0001 0xfffa 0x0014
c   0x0023 0x0006 0x0001 0xfff9 0x0015
c   0x0023 0x0006 0x0018 0xfff9 0x0016
c   0x0023 0x0006 0x0018 0xfff9 0x0017
c   0x0023 0x0006 0x0018 0xfff9 0x0008
c   0x0023 0x0006 0x0018 0xfff9 0x0009
c   0x0023 0x0006 0x0018 0xfff9 0x000a
c   0x0023 0x0006 0x0001 0xfff9 0x000b
c   0x0023 0x0006 0x0001 0xfff8 0x000c
c   0x0023 0x0006 0x0001 0xfff8 0x000d
c   0x0005 0x0006 0x0001 0xfff8 0x000e
c   0x0005 0x0006 0x0001 0xfff7 0x000f
c   0x0005 0x0006 0x0001 0xfff7 0x0010
c   0x0005 0x0005 0x0001 0xfff7 0x0011
c   0xfff8 0x0005 0x0001 0xfff7 0x0012
c   0x0023 0x0005 0x0001 0xfff7 0x0013
c   0x0024 0x0005 0x0001 0xfff7 0x0014
c   0x0024 0x0005 0x0001 0xfff6 0x0015
c   0x0024 0x0005 0x0018 0xfff6 0x0016
c   0x0024 0x0005 0x0018 0xfff6 0x0017
c   0x0024 0x0005 0x0018 0xfff6 0x0008
c   0x0024 0x0005 0x0018 0xfff6 0x0009
c   0x0024 0x0005 0x0018 0xfff6 0x000a
c   0x0024 0x0005 0x0001 0xfff6 0x000b
c   0x0024 0x0005 0x0001 0xfff5 0x000c
c   0x0024 0x0005 0x0001 0xfff5 0x000d
c   0x0006 0x0005 0x0001 0xfff5 0x000e
c   0x0006 0x0005 0x0001 0xfff4 0x000f
c   0x0006 0x0005 0x0001 0xfff4 0x0010
c   0x0006 0x0004 0x0001 0xfff4 0x0011
c   0xfff5 0x0004 0x0001 0xfff4 0x0012
c   0x0024 0x0004 0x0001 0xfff4 0x0013
c   0x0025 0x0004 0x0001 0xfff4 0x0014
c   0x0025 0x0004 0x0001 0xfff3 0x0015
c   0x0025 0x0004 0x0018 0xfff3 0x0016
c   0x0025 0x0004 0x0018 0xfff3 0x0017
c   0x0025 0x0004 0x0018 0xfff3 0x0008
c   0x0025 0x0004 0x0018 0xfff3 0x0009
c   0x0025 0x0004 0x0018 0xfff3 0x000a
c   0x0025 0x0004 0x0001 0xfff3 0x000b
c   0x0025 0x0004 0x0001 0xfff2 0x000c
c   0x0025 0x0004 0x0001 0xfff2 0x000d
c   0x0007 0x0004 0x0001 0xfff2 0x000e
c   0x0007 0x0004 0x0001 0xfff1 0x000f
c   0x0007 0x0004 0x0001 0xfff1 0x0010
c   0x0007 0x0003 0x0001 0xfff1 0x0011
c   0xfff2 0x0003 0x0001 0xfff1 0x0012
c   0x0025 0x0003 0x0001 0xfff1 0x0013
c   0x0026 0x0003 0x0001 0xfff1 0x0014
c   0x0026 0x0003 0x0001 0xfff0 0x0015
c   0x0026 0x0003 0x0018 0xfff0 0x0016
c   0x0026 0x0003 0x0018 0xfff0 0x0017
c   0x0026 0x0003 0x0018 0xfff0 0x0008
c   0x0026 0x0003 0x0018 0xfff0 0x0009
c   0x0026 0x0003 0x0018 0xfff0 0x000a
c   0x0026 0x0003 0x0001 0xfff0 0x000b
c   0x0026 0x0003 0x0001 0xffef 0x000c
c   0x0026 0x0003 0x0001 0xffef 0x000d
c   0x0008 0x0003 0x0001 0xffef 0x000e
c   0x0008 0x0003 0x0001 0xffee 0x000f
c   0x0008 0x0003 0x0001 0xffee 0x0010
c   0x0008 0x0002 0x0001 0xffee 0x0011
c   0xffef 0x0002 0x0001 0xffee 0x0012
c   0x0026 0x0002 0x0001 0xffee 0x0013
c   0x0027 0x0002 0x0001 0xffee 0x0014
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*/

/* Test case SUB:
CLK     R1     R2     R3     R4     PC

init R4=0x27;
init R2=0x93;
0        x      x      x      x 0x0000
c   0xff94 0x0093      x 0x0027 0x0001
c   0xff94 0x0093 0x006c 0x0027 0x0002
c   0xff94 0x00d8 0x006c 0x0027 0x0003
c   0xff94 0x00d8 0x006c 0xff28 0x0004

program(0x9142,0x9324,0x9231,0x9413)
*/

/* Test case MEM:
CLK     R1     R2     R3     R4     PC

0        x      x      x      x 0x0000
c   0x000a      x      x      x 0x0001
c   0x000a      x      x      x 0x0002
c   0x000a 0xba55      x      x 0x0003
c   0x000a 0xba55 0xba55      x 0x0004
c   0x000a 0xba55 0xba55 0x0005 0x0005
c   0x000f 0xba55 0xba55 0x0005 0x0006
c   0x000f 0xba5a 0xba55 0x0005 0x0007
c   0x000f 0xba5a 0xba55 0x0005 0x0008
c   0x000f 0xba5a 0xba55 0xba5a 0x0009

program(0x010a,0x9000,0x5210,0x5310,0x0405,0x8114,0x8224,0x4210,0x5410,0x0000,0xba55)
*/

/* Test case AND:
CLK     R1     R2     R3     R4     PC

init R1=0xF0AE;
init R3=0x0FCF;
0        x      x      x      x 0x0000
c   0xf0ae      x 0x0fcf 0x008e 0x0001
c   0xf0ae 0x008e 0x0fcf 0x008e 0x0002
c   0x008e 0x008e 0x0fcf 0x008e 0x0003

program(0xa413,0xa231,0xa124)
*/

/* Test case FIB:
CLK     R1     R2     R3     R4   FLAG     PC

declare FLAG = FL & 0xF;

0        x      x      x      x      x 0x0000
c   0x0001      x      x      x      x 0x0001
c   0x0001 0x0000      x      x      x 0x0002
c   0x0001 0x0000 0x0019      x      x 0x0003
c   0x0001 0x0000 0x0019      x 0x0004 0x0004
c   0x0001 0x0000 0x0019      x 0x0004 0x0005
c   0x0001 0x0000 0x0019 0x0001 0x0000 0x0006
c   0x0000 0x0000 0x0019 0x0001 0x0001 0x0007
c   0x0000 0x0001 0x0019 0x0001 0x0000 0x0008
c   0x0000 0x0001 0x0019 0x0001 0x0000 0x0009
c   0x0000 0x0001 0x0018 0x0001 0x0004 0x000a
c   0x0000 0x0001 0x0018 0x0001 0x0004 0x0003
c   0x0000 0x0001 0x0018 0x0001 0x0004 0x0004
c   0x0000 0x0001 0x0018 0x0001 0x0004 0x0005
c   0x0000 0x0001 0x0018 0x0001 0x0000 0x0006
c   0x0001 0x0001 0x0018 0x0001 0x0000 0x0007
c   0x0001 0x0001 0x0018 0x0001 0x0000 0x0008
c   0x0001 0x0001 0x0018 0x0001 0x0000 0x0009
c   0x0001 0x0001 0x0017 0x0001 0x0004 0x000a
c   0x0001 0x0001 0x0017 0x0001 0x0004 0x0003
c   0x0001 0x0001 0x0017 0x0001 0x0004 0x0004
c   0x0001 0x0001 0x0017 0x0001 0x0004 0x0005
c   0x0001 0x0001 0x0017 0x0002 0x0000 0x0006
c   0x0001 0x0001 0x0017 0x0002 0x0000 0x0007
c   0x0001 0x0002 0x0017 0x0002 0x0000 0x0008
c   0x0001 0x0002 0x0017 0x0001 0x0000 0x0009
c   0x0001 0x0002 0x0016 0x0001 0x0004 0x000a
c   0x0001 0x0002 0x0016 0x0001 0x0004 0x0003
c   0x0001 0x0002 0x0016 0x0001 0x0004 0x0004
c   0x0001 0x0002 0x0016 0x0001 0x0004 0x0005
c   0x0001 0x0002 0x0016 0x0003 0x0000 0x0006
c   0x0002 0x0002 0x0016 0x0003 0x0000 0x0007
c   0x0002 0x0003 0x0016 0x0003 0x0000 0x0008
c   0x0002 0x0003 0x0016 0x0001 0x0000 0x0009
c   0x0002 0x0003 0x0015 0x0001 0x0004 0x000a
c   0x0002 0x0003 0x0015 0x0001 0x0004 0x0003
c   0x0002 0x0003 0x0015 0x0001 0x0004 0x0004
c   0x0002 0x0003 0x0015 0x0001 0x0004 0x0005
c   0x0002 0x0003 0x0015 0x0005 0x0000 0x0006
c   0x0003 0x0003 0x0015 0x0005 0x0000 0x0007
c   0x0003 0x0005 0x0015 0x0005 0x0000 0x0008
c   0x0003 0x0005 0x0015 0x0001 0x0000 0x0009
c   0x0003 0x0005 0x0014 0x0001 0x0004 0x000a
c   0x0003 0x0005 0x0014 0x0001 0x0004 0x0003
c   0x0003 0x0005 0x0014 0x0001 0x0004 0x0004
c   0x0003 0x0005 0x0014 0x0001 0x0004 0x0005
c   0x0003 0x0005 0x0014 0x0008 0x0000 0x0006
c   0x0005 0x0005 0x0014 0x0008 0x0000 0x0007
c   0x0005 0x0008 0x0014 0x0008 0x0000 0x0008
c   0x0005 0x0008 0x0014 0x0001 0x0000 0x0009
c   0x0005 0x0008 0x0013 0x0001 0x0004 0x000a
c   0x0005 0x0008 0x0013 0x0001 0x0004 0x0003
c   0x0005 0x0008 0x0013 0x0001 0x0004 0x0004
c   0x0005 0x0008 0x0013 0x0001 0x0004 0x0005
c   0x0005 0x0008 0x0013 0x000d 0x0000 0x0006
c   0x0008 0x0008 0x0013 0x000d 0x0000 0x0007
c   0x0008 0x000d 0x0013 0x000d 0x0000 0x0008
c   0x0008 0x000d 0x0013 0x0001 0x0000 0x0009
c   0x0008 0x000d 0x0012 0x0001 0x0004 0x000a
c   0x0008 0x000d 0x0012 0x0001 0x0004 0x0003
c   0x0008 0x000d 0x0012 0x0001 0x0004 0x0004
c   0x0008 0x000d 0x0012 0x0001 0x0004 0x0005
c   0x0008 0x000d 0x0012 0x0015 0x0000 0x0006
c   0x000d 0x000d 0x0012 0x0015 0x0000 0x0007
c   0x000d 0x0015 0x0012 0x0015 0x0000 0x0008
c   0x000d 0x0015 0x0012 0x0001 0x0000 0x0009
c   0x000d 0x0015 0x0011 0x0001 0x0004 0x000a
c   0x000d 0x0015 0x0011 0x0001 0x0004 0x0003
c   0x000d 0x0015 0x0011 0x0001 0x0004 0x0004
c   0x000d 0x0015 0x0011 0x0001 0x0004 0x0005
c   0x000d 0x0015 0x0011 0x0022 0x0000 0x0006
c   0x0015 0x0015 0x0011 0x0022 0x0000 0x0007
c   0x0015 0x0022 0x0011 0x0022 0x0000 0x0008
c   0x0015 0x0022 0x0011 0x0001 0x0000 0x0009
c   0x0015 0x0022 0x0010 0x0001 0x0004 0x000a
c   0x0015 0x0022 0x0010 0x0001 0x0004 0x0003
c   0x0015 0x0022 0x0010 0x0001 0x0004 0x0004
c   0x0015 0x0022 0x0010 0x0001 0x0004 0x0005
c   0x0015 0x0022 0x0010 0x0037 0x0000 0x0006
c   0x0022 0x0022 0x0010 0x0037 0x0000 0x0007
c   0x0022 0x0037 0x0010 0x0037 0x0000 0x0008
c   0x0022 0x0037 0x0010 0x0001 0x0000 0x0009
c   0x0022 0x0037 0x000f 0x0001 0x0004 0x000a
c   0x0022 0x0037 0x000f 0x0001 0x0004 0x0003
c   0x0022 0x0037 0x000f 0x0001 0x0004 0x0004
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*/

/* Test case ORR:
CLK     R1     R2     R3     R4     PC

init R4=0xF0AE;
init R3=0x0FC8;
0        x      x      x      x 0x0000
c   0xffee      x 0x0fc8 0xf0ae 0x0001
c   0xffee 0xffee 0x0fc8 0xf0ae 0x0002

program(0xb143,0xb234)
*/

/* Test case COND:
CLK     R1     R2     R3     R4     PC

0        x      x      x      x 0x0000
c   0x0000      x      x      x 0x0001
c   0x0000 0x0000      x      x 0x0002
c   0x0000 0x0000 0x0016      x 0x0003
c   0x0000 0x0000 0x0016 0x0001 0x0004
c   0x0000 0x0000 0x0016 0x0001 0x0005
c   0x0000 0x0001 0x0016 0x0001 0x0006
c   0x0000 0x0001 0x0016 0x0001 0x0007
c   0x0000 0x0001 0x0016 0x0001 0x0008
c   0x0000 0x0001 0x0016 0x0001 0x0009
c   0x0000 0x0001 0x0016 0x0001 0x000a
c   0x1337 0x0001 0x0016 0x0001 0x000b
c   0x1337 0x0001 0x0017 0x0001 0x000c
c   0x1337 0x0001 0x0017 0x0001 0x000d
c   0x1337 0x0000 0x0017 0x0001 0x000e
c   0x1337 0x0000 0x0017 0x0001 0x000f
c   0x1337 0x0000 0x0017 0x0001 0x0010
c   0x1337 0x1337 0x0017 0x0001 0x0011
c   0x1337 0x1337 0x0017 0x0001 0x0012
c   0x1337 0x1337 0x0017 0x0001 0x0013
c   0x1337 0x1337 0x0017 0x0001 0x0014
c   0x0051 0x1337 0x0017 0x0001 0x0015

program(0x0100,0x0200,0x0316,0x0401,0x8000,0x8a04,0xb944,0x9040,0x5930,0x9000,0x5930,0x8334,0x4930,0x5230,0x9000,0x4930,0x5230,0x9040,0x0915,0x9000,0x0951,0x0000,0x1337)
*/
