// Digital circuit reg_file-extended.dig as structural Verilog
module reg_file_extended (
  input  [2:0] RS1,
  input  [2:0] RS2,
  input  [2:0] WS,
  input  WE,
  input  [15:0] IN,
  input  clk,
  input  [15:0] f1,
  input  [15:0] PC,
  input  SETH,
  input  [2:0] RS3,
  input  [15:0] Stack,
  input  SMOV,
  input  TMPWRITE,
  output [15:0] OUT2,
  output PCWRITE,
  output [15:0] OUT1,
  output f1write,
  output [15:0] OUT3
);

  wire and_1_out, and_2_out, and_3_out, and_4_out, and_5_out, and_6_out, and_7_out, and_8_out, and_9_out,
       demultiplexer_1_out_1, demultiplexer_2_out_1, demultiplexer_3_out_0, demultiplexer_3_out_1,
       demultiplexer_3_out_2, demultiplexer_3_out_3, demultiplexer_3_out_4, demultiplexer_3_out_5,
       demultiplexer_3_out_6, demultiplexer_3_out_7, not_1_out;
  wire [15:0] multiplexer_1_out, multiplexer_2_out, multiplexer_3_out, multiplexer_4_out, multiplexer_6_out,
       multiplexer_7_out, multiplexer_8_out, multiplexer_10_out, multiplexer_11_out, multiplexer_12_out,
       multiplexer_14_out, multiplexer_15_out, R1_q, R2_q, R3_q, R4_q, R5_q, R6_q, R7_q, RZ_q;

  and and_1 (and_1_out, WE, not_1_out);
  not not_1 (not_1_out, TMPWRITE);
  and and_2 (and_2_out, demultiplexer_3_out_7, and_1_out);
  Demultiplexer demultiplexer_1 (.sel(SMOV), .in(and_2_out), .out_0(PCWRITE), .out_1(demultiplexer_1_out_1));
  and and_3 (and_3_out, demultiplexer_3_out_6, and_1_out);
  and and_4 (and_4_out, demultiplexer_3_out_4, and_1_out);
  and and_5 (and_5_out, demultiplexer_3_out_5, and_1_out);
  Demultiplexer demultiplexer_2 (.sel(SMOV), .in(and_5_out), .out_0(f1write), .out_1(demultiplexer_2_out_1));
  and and_6 (and_6_out, demultiplexer_3_out_3, and_1_out);
  Multiplexer #(.Bits(16)) multiplexer_1 (
    .sel(SETH), .in_0(IN), .in_1({IN[7:0], multiplexer_15_out[7:0]}), .out(multiplexer_1_out));
  Demultiplexer #(.Selector_Bits(3)) demultiplexer_3 (
    .sel(WS), .in(1'b1), .out_0(demultiplexer_3_out_0), .out_1(demultiplexer_3_out_1),
    .out_2(demultiplexer_3_out_2), .out_3(demultiplexer_3_out_3), .out_4(demultiplexer_3_out_4),
    .out_5(demultiplexer_3_out_5), .out_6(demultiplexer_3_out_6), .out_7(demultiplexer_3_out_7));
  and and_7 (and_7_out, demultiplexer_3_out_2, and_1_out);
  and and_8 (and_8_out, demultiplexer_3_out_0, and_1_out);
  and and_9 (and_9_out, demultiplexer_3_out_1, and_1_out);
  Register #(.Bits(16)) RZ (.D({16{1'b0}}), .C(clk), .en(and_8_out), .Q(RZ_q));
  Register #(.Bits(16)) R1 (.D(multiplexer_1_out), .C(clk), .en(and_9_out), .Q(R1_q));
  Register #(.Bits(16)) R2 (.D(multiplexer_1_out), .C(clk), .en(and_7_out), .Q(R2_q));
  Register #(.Bits(16)) R3 (.D(multiplexer_1_out), .C(clk), .en(and_6_out), .Q(R3_q));
  Register #(.Bits(16)) R4 (.D(multiplexer_1_out), .C(clk), .en(and_4_out), .Q(R4_q));
  Register #(.Bits(16)) R5 (.D(multiplexer_1_out), .C(clk), .en(demultiplexer_2_out_1), .Q(R5_q));
  Register #(.Bits(16)) R6 (.D(multiplexer_1_out), .C(clk), .en(and_3_out), .Q(R6_q));
  Register #(.Bits(16)) R7 (.D(multiplexer_1_out), .C(clk), .en(demultiplexer_1_out_1), .Q(R7_q));
  Multiplexer #(.Bits(16)) multiplexer_2 (.sel(SMOV), .in_0(PC), .in_1(R7_q), .out(multiplexer_2_out));
  Multiplexer #(.Bits(16)) multiplexer_3 (.sel(SMOV), .in_0(Stack), .in_1(R6_q), .out(multiplexer_3_out));
  Multiplexer #(.Bits(16)) multiplexer_4 (.sel(SMOV), .in_0(f1), .in_1(R5_q), .out(multiplexer_4_out));
  // NotConnected on nothing
  Multiplexer #(.Selector_Bits(3), .Bits(16)) multiplexer_5 (
    .sel(RS2), .in_0(RZ_q), .in_1(R1_q), .in_2(R2_q), .in_3(R3_q), .in_4(R4_q), .in_5(multiplexer_4_out),
    .in_6(multiplexer_3_out), .in_7(multiplexer_2_out), .out(OUT2));
  Multiplexer #(.Bits(16)) multiplexer_6 (.sel(SMOV), .in_0(PC), .in_1(R7_q), .out(multiplexer_6_out));
  Multiplexer #(.Bits(16)) multiplexer_7 (.sel(SMOV), .in_0(Stack), .in_1(R6_q), .out(multiplexer_7_out));
  Multiplexer #(.Bits(16)) multiplexer_8 (.sel(SMOV), .in_0(f1), .in_1(R5_q), .out(multiplexer_8_out));
  Multiplexer #(.Selector_Bits(3), .Bits(16)) multiplexer_9 (
    .sel(RS1), .in_0(RZ_q), .in_1(R1_q), .in_2(R2_q), .in_3(R3_q), .in_4(R4_q), .in_5(multiplexer_8_out),
    .in_6(multiplexer_7_out), .in_7(multiplexer_6_out), .out(OUT1));
  // NotConnected on nothing
  Multiplexer #(.Bits(16)) multiplexer_10 (.sel(SMOV), .in_0(PC), .in_1(R7_q), .out(multiplexer_10_out));
  Multiplexer #(.Bits(16)) multiplexer_11 (.sel(SMOV), .in_0(Stack), .in_1(R6_q), .out(multiplexer_11_out));
  Multiplexer #(.Bits(16)) multiplexer_12 (.sel(SMOV), .in_0(f1), .in_1(R5_q), .out(multiplexer_12_out));
  Multiplexer #(.Selector_Bits(3), .Bits(16)) multiplexer_13 (
    .sel(RS3), .in_0(RZ_q), .in_1(R1_q), .in_2(R2_q), .in_3(R3_q), .in_4(R4_q), .in_5(multiplexer_12_out),
    .in_6(multiplexer_11_out), .in_7(multiplexer_10_out), .out(OUT3));
  // NotConnected on nothing
  Multiplexer #(.Selector_Bits(3), .Bits(16)) multiplexer_14 (
    .sel(WS), .in_0(RZ_q), .in_1(R1_q), .in_2(R2_q), .in_3(R3_q), .in_4(R4_q), .in_5(R5_q), .in_6(R6_q),
    .in_7(R7_q), .out(multiplexer_14_out));
  Multiplexer #(.Bits(16)) multiplexer_15 (
    .sel(SETH), .in_0({16{1'b0}}), .in_1(multiplexer_14_out), .out(multiplexer_15_out));

  // Other names for the same wires on the sheet: input[15:0] = IN

  // Notes on the sheet:
  //   RS1: The index of the register which should output its value to OUT1.
  //   RS2: The index of the register which should output its value to OUT2.
  //   WS: The index of the register which should save the value on IN on the next clock cycle (if WE is high).
  //   WE: Whether the register selected by WS should save the value from IN on the next cycle.
  //   IN: The value to be saved into the register specified by WS if WE is high,
  //   OUT2: The value in the register specified by RS2.
  //   f1: The value to be saved into the register specified by WS if WE is high,
  //   PC: The value to be saved into the register specified by WS if WE is high,
  //   SETH: The value to be saved into the register specified by WS if WE is high,
  //   OUT1: The value in the register specified by RS2.
  //   OUT3: The value in the register specified by RS2.
  //   RS3: The index of the register which should output its value to OUT2.
  //   Stack: The value to be saved into the register specified by WS if WE is high,
  //   SMOV: Whether the register selected by WS should save the value from IN on the next cycle.
  //   TMPWRITE: Whether the register selected by WS should save the value from IN on the next cycle.
  //   Takes last 3 bits
endmodule

/* Test case:
clk RS1 RS2 WS WE IN OUT1 OUT2
c 0 0 0 1 0x1234 0x0000 0x0000
c 1 0 1 1 0xBEEF 0xBEEF 0x0000
c 2 1 2 1 0xDEAD 0xDEAD 0xBEEF
c 3 2 3 1 0xFFFF 0xFFFF 0xDEAD
c 3 2 3 0 0xABCD 0xFFFF 0xDEAD
c 3 2 2 0 0xABCD 0xFFFF 0xDEAD
c 1 0 1 0 0xABCD 0xBEEF 0x0000
c 1 0 0 0 0xABCD 0xBEEF 0x0000
c 1 0 2 1 0xBADE 0xBEEF 0x0000
c 0 2 2 1 0xBADE 0x0000 0xBADE
c 0 0 2 0 0x1234 0x0000 0x0000
c 2 3 0 1 0x0000 0xBADE 0xFFFF
c 0 0 2 0 0x1234 0x0000 0x0000
*/
