// Digital circuit reg_file1.dig as structural Verilog
module reg_file1 (
  input  [2:0] RS1,
  input  [2:0] RS2,
  input  [2:0] WS,
  input  WE,
  input  [15:0] IN,
  input  clk,
  input  [15:0] f1,
  input  [15:0] PC,
  input  SETH,
  output [15:0] OUT2,
  output PCWRITE,
  output [15:0] OUT1
);

  wire and_2_out, and_3_out, and_4_out, and_5_out, and_6_out, demultiplexer_1_out_0, demultiplexer_1_out_1,
       demultiplexer_1_out_2, demultiplexer_1_out_3, demultiplexer_1_out_4, demultiplexer_1_out_7, not_1_out;
  wire [15:0] multiplexer_1_out, multiplexer_2_out, multiplexer_3_out, R1_q, R2_q, R3_q, R4_q, RZ_q;

  not not_1 (not_1_out, clk);
  and and_1 (PCWRITE, demultiplexer_1_out_7, WE);
  and and_2 (and_2_out, demultiplexer_1_out_4, WE);
  and and_3 (and_3_out, demultiplexer_1_out_3, WE);
  Multiplexer #(.Bits(16)) multiplexer_1 (
    .sel(SETH), .in_0(IN), .in_1({IN[7:0], multiplexer_2_out[7:0]}), .out(multiplexer_1_out));
  Demultiplexer #(.Selector_Bits(3)) demultiplexer_1 (
    .sel(WS), .in(1'b1), .out_0(demultiplexer_1_out_0), .out_1(demultiplexer_1_out_1),
    .out_2(demultiplexer_1_out_2), .out_3(demultiplexer_1_out_3), .out_4(demultiplexer_1_out_4),
    .out_7(demultiplexer_1_out_7));  // open: out_5, out_6
  and and_4 (and_4_out, demultiplexer_1_out_2, WE);
  and and_5 (and_5_out, demultiplexer_1_out_0, WE);
  and and_6 (and_6_out, demultiplexer_1_out_1, WE);
  Register #(.Bits(16)) RZ (.D({16{1'b0}}), .C(not_1_out), .en(and_5_out), .Q(RZ_q));
  Register #(.Bits(16)) R1 (.D(multiplexer_1_out), .C(not_1_out), .en(and_6_out), .Q(R1_q));
  Register #(.Bits(16)) R2 (.D(multiplexer_1_out), .C(not_1_out), .en(and_4_out), .Q(R2_q));
  Register #(.Bits(16)) R3 (.D(multiplexer_1_out), .C(not_1_out), .en(and_3_out), .Q(R3_q));
  Register #(.Bits(16)) R4 (.D(multiplexer_1_out), .C(not_1_out), .en(and_2_out), .Q(R4_q));
  Multiplexer #(.Bits(16)) multiplexer_2 (
    .sel(SETH), .in_0({16{1'b0}}), .in_1(multiplexer_3_out), .out(multiplexer_2_out));
  Multiplexer #(.Selector_Bits(3), .Bits(16)) multiplexer_3 (
    .sel(WS), .in_0(RZ_q), .in_1(R1_q), .in_2(R2_q), .in_3(R3_q), .in_4(R4_q), .in_5(PC), .in_6({16{1'b0}}),
    .in_7(f1), .out(multiplexer_3_out));
  // NotConnected on nothing
  Multiplexer #(.Selector_Bits(3), .Bits(16)) multiplexer_4 (
    .sel(RS2), .in_0(RZ_q), .in_1(R1_q), .in_2(R2_q), .in_3(R3_q), .in_4(R4_q), .in_5(f1), .in_6({16{1'b0}}),
    .in_7(PC), .out(OUT2));
  Multiplexer #(.Selector_Bits(3), .Bits(16)) multiplexer_5 (
    .sel(RS1), .in_0(RZ_q), .in_1(R1_q), .in_2(R2_q), .in_3(R3_q), .in_4(R4_q), .in_5(f1), .in_6({16{1'b0}}),
    .in_7(PC), .out(OUT1));
  // NotConnected on nothing

  // Other names for the same wires on the sheet: input[15:0] = IN

  // Notes on the sheet:
  //   RS1: The index of the register which should output its value to OUT1.
  //   RS2: The index of the register which should output its value to OUT2.
  //   WS: The index of the register which should save the value on IN on the next clock cycle (if WE is high).
  //   WE: Whether the register selected by WS should save the value from IN on the next cycle.
  //   IN: The value to be saved into the register specified by WS if WE is high,
  //   OUT2: The value in the register specified by RS2.
  //   f1: The value to be saved into the register specified by WS if WE is high,
  //   PC: The value to be saved into the register specified by WS if WE is high,
  //   SETH: The value to be saved into the register specified by WS if WE is high,
  //   OUT1: The value in the register specified by RS2.
  //   Takes last 3 bits
endmodule

/* Test case:
clk RS1 RS2 WS WE IN OUT1 OUT2
c 0 0 0 1 0x1234 0x0000 0x0000
c 1 0 1 1 0xBEEF 0xBEEF 0x0000
c 2 1 2 1 0xDEAD 0xDEAD 0xBEEF
c 3 2 3 1 0xFFFF 0xFFFF 0xDEAD
c 3 2 3 0 0xABCD 0xFFFF 0xDEAD
c 3 2 2 0 0xABCD 0xFFFF 0xDEAD
c 1 0 1 0 0xABCD 0xBEEF 0x0000
c 1 0 0 0 0xABCD 0xBEEF 0x0000
c 1 0 2 1 0xBADE 0xBEEF 0x0000
c 0 2 2 1 0xBADE 0x0000 0xBADE
c 0 0 2 0 0x1234 0x0000 0x0000
c 2 3 0 1 0x0000 0xBADE 0xFFFF
c 0 0 2 0 0x1234 0x0000 0x0000
*/
